# Fritzing sketch sketch (saved by Fritzing 0.9.3b)
breadboards: 2

parts:
  ARDUINO = Arduino Uno (Rev3)
  AM2302 = Humidity and Temperature Sensor RHT03
  R1 = Resistor [tolerance=±5% resistance=10k package=THT]
  BMP180 = Barometric Pressure Sensor - BMP180 Breakout (GY-68)
  LCD1602 = LCD screen

nets:
  N1: ARDUINO.D8, LCD1602.RS
  N2: ARDUINO.D9_PWM, LCD1602.E
  N3: ARDUINO.A4/SDA, BMP180.SDA
  N4: ARDUINO.A5/SCL, BMP180.SCL
  N5: ARDUINO.D2, AM2302.Data-signal, R1.Pin_1
  N6: ARDUINO.D4, LCD1602.DB4
  N7: ARDUINO.D5_PWM, LCD1602.DB5
  N8: ARDUINO.D6_PWM, LCD1602.DB6
  N9: ARDUINO.D7, LCD1602.DB7
  3V3: ARDUINO.3V3, BMP180.VCC, LCD1602.VDD
  5V: ARDUINO.5V, AM2302.Vcc, R1.Pin_0, LCD1602.LED+
  GND: ARDUINO.GND, AM2302.GND_2, BMP180.GND, LCD1602.VSS, LCD1602.V0, LCD1602.R/W, LCD1602.LED-
